# Fritzing sketch t-gauge-automation-schematic (saved by Fritzing 1.0.5)
breadboards: 1

parts:
  Part3 = Adafruit DRV8833 DC/Stepper Motor Driver [part_number="Adafruit #3297"]
  Raspberry_Pi_1 = Raspberry Pi 3 [part_number=RPI-3-V1.2]
  M1 = DC Motor [voltage_(max)=6V voltage_(min)=3V]

nets:
  N1: Part3.PWRIN, Raspberry_Pi_1.5V
  GND: Part3.GND, Raspberry_Pi_1.GND
  N2: Part3.AOUT2, M1.pin_1
  N3: Part3.AOUT1, M1.pin_2
  N4: Part3.!SLEEP, Raspberry_Pi_1.3v3
  N5: Part3.AIN2, Raspberry_Pi_1.GIPO27
  N6: Part3.AIN1, Raspberry_Pi_1.GIPO22

custom parts:
  Adafruit DRV8833 DC/Stepper Motor Driver: Spin two DC motors or step one bi-polar or uni-polar stepper with up to 1.2A per channel using the DRV8833. This motor driver chip is a nice alternative to the TB6612 driver. Like that chip, you get 2 full H-bridges, but this chip is better for low voltage uses (can run from 2.7V up to 10.8V motor power) and has built in current limiting capability. We set it up for 1A current limiting so you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
